# Fritzing sketch zero_obd (saved by Fritzing 0.9.4)
circuit board: 8.46667cm x 5.64444cm
breadboards: 1

parts:
  J2 = female pin header, 4 pins [form="♀ (female)"]
  J3 = Screw terminal - 2 pins [package=THT]
  J4 = Screw terminal - 2 pins [package=THT]
  J5 = Screw terminal - 2 pins [package=THT]
  J6 = Screw terminal - 2 pins [package=THT]
  J1 = female pin header, 4 pins [form="♀ (female)"]

nets:
  N1: J2.pin1, J5.pin1
  N2: J2.pin2, J2.pin4, J3.pin1
  N3: J3.pin2, J4.pin1, J6.pin1, J1.pin1
  N4: J5.pin2, J1.pin4
  N5: J6.pin2, J1.pin3

notes:
  Inbound power terminals
  black is ground, red is 3.3V
  J1/J2 headers for ESP-01 module.
  ground to j1-1, board hangs over to the right
  Optional garage door opener button terminals
  Terminals to connect to OBD-II pins: ground, TX, and RX
